# Fritzing sketch lcd_rfid_motion_servo (saved by Fritzing 0.9.10b)
breadboards: 1

parts:
  Part1 = RFID-RC522-v2
  Mod1 = Amica NodeMCU DEVKIT 1.0
  Part2 = LCD1602-I2C
  J1 = Basic Servo
  PIR1 = PIR sensor

nets:
  N1: Part1.SDA, Mod1.pin5
  N2: Part1.SCK, Mod1.pin8
  N3: Part1.MOSI, Mod1.pin6
  N4: Part1.MISO, Mod1.pin7
  GND: Part1.GND, Part2.GND, J1.gnd, PIR1.GND
  N5: Part1.RST, Mod1.pin_15
  VCC: Part1.3.3V, Mod1.pin1, Mod1.pin2, Mod1.pin_9, Mod1.pin_10, Mod1.pin_25, Mod1.pin_26, Mod1.pin_29, Part2.VCC, J1.vcc, PIR1.VDD
  N6: Mod1.pin_11, J1.pulse
  N7: Mod1.pin_12, PIR1.SIG
  N8: Mod1.pin_13, Part2.SDA
  N9: Mod1.pin_14, Part2.SCL

custom parts:
  RFID-RC522-v2: A simple China made RFID-RC522 Reader; do check the pin labels, as this is a MFRC522 based clone.
  LCD1602-I2C: A standard character display, usually with 2x16 characters. Comes in many colors with LCM1602 IIC attached.
