# Fritzing sketch lcd_servo (saved by Fritzing 0.9.10b)
breadboards: 1

parts:
  Mod1 = Amica NodeMCU DEVKIT 1.0
  Part2 = LCD1602-I2C
  J1 = Basic Servo
  LED2 = RGB LED (com. anode, rbg) [package="5 mm [THT]"]
  buz1 = Piezo Buzzer
  R1 = Resistor [tolerance=±5% resistance=220 package="2512 [SMD]"]

nets:
  VCC: Mod1.pin1, Mod1.pin_10, Mod1.pin_26, Part2.VCC, J1.vcc
  GND: Mod1.pin2, Mod1.pin_9, Mod1.pin_25, Mod1.pin_29, Part2.GND, J1.gnd, buz1.pin_2, R1.Pin_0
  N1: Mod1.pin6, J1.pulse
  N2: Mod1.pin7, Part2.SDA
  N3: Mod1.pin8, Part2.SCL
  N4: Mod1.pin_11, buz1.pin_1
  N5: Mod1.pin_13, LED2.red_cathode
  N6: Mod1.pin_14, LED2.green_cathode
  N7: LED2.blue_cathode, R1.Pin_1

custom parts:
  LCD1602-I2C: A standard character display, usually with 2x16 characters. Comes in many colors with LCM1602 IIC attached.
  Piezo Buzzer: Part from https://www.nutsvolts.com/magazine/article/november2012_SmileysWorkshop. Breadboard and icon images modified to be 0.3" in spacing and be more similar to the actual physical part.
